# Fritzing sketch Access Control (saved by Fritzing 0.9.3b)
breadboards: 1

parts:
  Part1 = Arduino Mega 2560 (Rev3)
  S1 = Square Pushbutton
  S2 = Momentary Switch [package=ksa_sealed_tac_switch]
  S3 = Momentary Switch [package=ksa_sealed_tac_switch]
  LED2 = smd LED [color="Green (555nm)" package="0603 [SMD]"]
  LCM1602_IIC1 = LCM1602 IIC [part_number="LCM1602 IIC" chip_label="LCM1602 IIC" package="DIP (Dual Inline) [THT]"]
  U1 = LCD-16X2 [package=lcd-16x2]
  Part2 = KY-016 RGB Full Color LED Module [package="Breakout board"]
  Part3 = KY-032 IR Obstacle Avoidance Sensor Module [package="Breakout board"]
  Part4 = RFID-RC522-v2
  KY-1 = Keyes Relay [package=THT]
  Part5 = KY-006 Passive Buzzer Module [package="Breakout board"]
  R1 = Resistor [tolerance=±5% resistance=1k package=THT]
  R2 = Resistor [tolerance=±5% resistance=1k package=THT]
  R3 = Resistor [tolerance=±5% resistance=1k package=THT]
  L2 = Solenoid
  U3 = LIPO-2000mAh [package=lipo-2000]
  Keypad4x1 = Keypad Membran 4x4
  U4 = LM2596 step down module

nets:
  N1: Part1.A0, Part3.out
  N2: Part1.D21/SCL, LCM1602_IIC1.SCL
  N3: Part1.D20/SDA, LCM1602_IIC1.SDA
  N4: Part1.D19/RX1, S3.1
  N5: Part1.D18/TX1, S2.1
  N6: Part1.D13_PWM, LED2.anode
  N7: Part1.D12_PWM, Part5.S
  N8: Part1.D11_PWM, KY-1.signal
  3V3: Part1.3V3, Part4.3.3V
  5V: Part1.5V, S1.leg1, S2.3, S3.3, LCM1602_IIC1.VCC, Part3.+, KY-1.power
  N9: Part1.VIN, L2.pin2, U4.OUT+
  N10: Part1.D2_PWM, Part4.RST
  N11: Part1.D3_PWM, S1.leg0, R3.Pin_0
  N12: Part1.D5_PWM, Part2.R
  N13: Part1.D6_PWM, Part2.G
  N14: Part1.D7_PWM, Part2.B
  N15: Part1.D38, Keypad4x1.Pin8
  N16: Part1.D39, Keypad4x1.Pin4
  N17: Part1.D40, Keypad4x1.Pin7
  N18: Part1.D41, Keypad4x1.Pin3
  N19: Part1.D42, Keypad4x1.Pin6
  N20: Part1.D43, Keypad4x1.Pin2
  N21: Part1.D44, Keypad4x1.Pin5
  N22: Part1.D45, Keypad4x1.Pin1
  N23: Part1.D50, Part4.MISO
  N24: Part1.D51, Part4.MOSI
  N25: Part1.D52, Part4.SCK
  N26: Part1.D53, Part4.SDA
  N27: S2.2, R1.Pin_0
  N28: S3.2, R2.Pin_0
  GND: LED2.cathode, LCM1602_IIC1.GND, Part2.-, Part3.GND, Part4.GND, KY-1.ground, KY-1.NO, Part5.-, R1.Pin_1, R3.Pin_1, U3.-, U4.IN-, U4.OUT-
  VSS: LCM1602_IIC1.VSS, U1.VSS
  VDD: LCM1602_IIC1.VDD, U1.VDD
  N29: LCM1602_IIC1.V0, U1.VO
  N30: LCM1602_IIC1.RS, U1.RS
  N31: LCM1602_IIC1.RW, U1.R_W
  N32: LCM1602_IIC1.E, U1.E
  N33: LCM1602_IIC1.D0, U1.DB0
  N34: LCM1602_IIC1.D1, U1.DB1
  N35: LCM1602_IIC1.D2, U1.DB2
  N36: LCM1602_IIC1.D3, U1.DB3
  N37: LCM1602_IIC1.D4, U1.DB4
  N38: LCM1602_IIC1.D5, U1.DB5
  N39: LCM1602_IIC1.D6, U1.DB6
  N40: LCM1602_IIC1.D7, U1.DB7
  N41: LCM1602_IIC1.A, U1.A
  N42: LCM1602_IIC1.K, U1.K
  N43: KY-1.C, L2.pin1
  N44: U3.+, U4.IN+

custom parts:
  LCM1602 IIC: I2C-Module to use a 1602 or 2004 LCD on with the wire.h libory Serial LCD Modul
  KY-016 RGB Full Color LED Module: KY-016 Arduino full color 5mm RGB LED, different colors can be obtained by mixing the three primary colors.
  KY-032 IR Obstacle Avoidance Sensor Module: Distance-adjustable, infrared proximity sensor designed for wheeled robots. Also known as AD-032.
  RFID-RC522-v2: A simple China made RFID-RC522 Reader; do check the pin labels, as this is a MFRC522 based clone.
  Keyes Relay: The Keyes 5V relay module is suitable for SCM development, home appliance control. It uses a 5V~12V TIL control signal which can control DC / AC signal.
  KY-006 Passive Buzzer Module: Passive Piezoelectric Buzzer Module Keyes KY-006, it can produce a range of sound tones depending on the input frequency.
  Keypad Membran 4x4: Membrane Keypad 4x4 Matrix
  LM2596 step down module: LM2596 DC-DC step down power supply module 3 A.
